# Fritzing sketch Water Level (saved by Fritzing 0.9.7b)

parts:
  Part3 = Arduino Nano (Rev3.0)
  LCM1602_IIC1 = LCM1602 IIC [part_number="LCM1602 IIC" chip_label="LCM1602 IIC" package="DIP (Dual Inline) [THT]"]
  U1 = LCD-16X2 [package=lcd-16x2_noholes]
  KY-1 = Keyes Relay [package=THT]
  J1 = Power Jack [package=power_jack_pth_lock]
  HC-SR04_Sensor_1 = HC-SR04 Ultrasonic Distance Sensor
  M1 = DC Motor
  Mod1 = Passive Buzzer
  M2 = RioRand LM2596
  J2 = Power Jack [package=power_jack_pth_lock]

nets:
  N1: Part3.D2, HC-SR04_Sensor_1.ECHO
  N2: Part3.D3, HC-SR04_Sensor_1.TRIG
  N3: Part3.D4, KY-1.signal
  N4: Part3.D5, Mod1.S
  GND: Part3.GND, LCM1602_IIC1.GND, KY-1.ground, HC-SR04_Sensor_1.GND, Mod1.-, M2.Pin_4
  VCC: Part3.5V, LCM1602_IIC1.VCC, KY-1.power, HC-SR04_Sensor_1.VCC, Mod1.NC, M2.Pin_3
  N5: Part3.A5, LCM1602_IIC1.SCL
  N6: Part3.A4, LCM1602_IIC1.SDA
  VSS: LCM1602_IIC1.VSS, U1.VSS
  VDD: LCM1602_IIC1.VDD, U1.VDD
  N7: LCM1602_IIC1.V0, U1.VO
  N8: LCM1602_IIC1.RS, U1.RS
  N9: LCM1602_IIC1.RW, U1.R_W
  N10: LCM1602_IIC1.E, U1.E
  N11: LCM1602_IIC1.D0, U1.DB0
  N12: LCM1602_IIC1.D1, U1.DB1
  N13: LCM1602_IIC1.D2, U1.DB2
  N14: LCM1602_IIC1.D3, U1.DB3
  N15: LCM1602_IIC1.D4, U1.DB4
  N16: LCM1602_IIC1.D5, U1.DB5
  N17: LCM1602_IIC1.D6, U1.DB6
  N18: LCM1602_IIC1.D7, U1.DB7
  N19: LCM1602_IIC1.A, U1.A
  N20: LCM1602_IIC1.K, U1.K
  N21: LCM1602_IIC1.LED_A, LCM1602_IIC1.LED_B
  N22: KY-1.NC, M1.pin_1
  N23: KY-1.C, J1.PWR
  N24: J1.GND, M1.pin_2
  N25: M2.Pin_1, J2.PWR
  N26: M2.Pin_2, J2.GND

custom parts:
  LCM1602 IIC: I2C-Module to use a 1602 or 2004 LCD on with the wire.h libory Serial LCD Modul
  Keyes Relay: The Keyes 5V relay module is suitable for SCM development, home appliance control. It uses a 5V~12V TIL control signal which can control DC / AC signal.
